// Logisim project Devices.circ as structural Verilog: 2 circuits, main circuit ButtonAdapter
module ButtonAdapter (
  input  BUTTON_IN,
  input  [7:0] DBUS_IN,
  input  [15:0] ABUS,
  input  NOT_DEVICE_IN,
  input  NOT_DEVICE_OUT,
  input  CLK,
  output NOT_IRQ,
  output [7:0] D_BUS_OUT
);

  wire not_1_out, not_2_out;
  wire [0:0] s_r_ff_1_q;

  S_R_Flip_Flop s_r_ff_1 (.S(BUTTON_IN), .R(not_1_out), .clk(CLK), .Q(s_r_ff_1_q[0]));  // open: reset, Qn, preset
  not not_1 (not_1_out, NOT_DEVICE_IN);
  assign NOT_IRQ = s_r_ff_1_q[0] ? 1'b0 : 1'bz;  // Controlled_Buffer controlled_buffer_1
  assign D_BUS_OUT = not_2_out ? {{7{1'b0}}, s_r_ff_1_q[0]} : 8'bz;  // Controlled_Buffer controlled_buffer_2
  not not_2 (not_2_out, NOT_DEVICE_OUT);
endmodule

module HexDisplayAdapter (
  input  [7:0] DBUS_IN,
  input  [15:0] ABUS,
  input  NOT_DEVICE_IN,
  input  NOT_DEVICE_OUT,
  input  CLK,
  output [3:0] LSB,
  output [3:0] MSB
);

  wire not_1_out;

  Register register_1 (.D(DBUS_IN), .en(not_1_out), .clk(CLK), .Q({MSB, LSB}));  // open: clr
  not not_1 (not_1_out, NOT_DEVICE_IN);
endmodule
