// Logisim project Computer8Bit.circ as structural Verilog: 21 circuits, main circuit main
module main (
);

  wire ADDR_SEL0, ADDR_SEL1, C1, C2, C3, C4, CSPC_DIR, FLAGS_MODE_SEL0, FLAGS_MODE_SEL1, FLAGS_MODE_SEL2, J,
       JA, JC, JN, JZ, keyboard_1_avail, keyboardadapter_1_k_clear, keyboardadapter_1_k_clk,
       keyboardadapter_1_k_read_en, nor_1_out, nor_2_out, nor_3_out, nor_4_out, not_1_out, not_2_out,
       not_3_out, not_4_out, not_5_out, not_6_out, not_7_out, not_8_out, not_9_out, not_10_out, not_11_out,
       NOT_ABH_IN, NOT_ABL_IN, NOT_CS_IN, NOT_CS_OUT, NOT_DATA_LATCH_OUT, NOT_DEVICE_IN, NOT_DEVICE_OUT,
       NOT_DEVICE_SEL_0, NOT_DEVICE_SEL_1, NOT_DEVICE_SEL_2, NOT_DEVICE_SEL_3, NOT_DEVICE_SEL_4,
       NOT_DEVICE_SEL_5, NOT_DEVICE_SEL_RAM, NOT_DEVICE_SEL_ROM, NOT_FETCH, NOT_FLAGS_OUT, NOT_HLT, NOT_IRQ,
       NOT_IVH_OUT, NOT_IVL_OUT, NOT_PASS, NOT_PC_IN, NOT_PC_INC, NOT_PC_OUT, NOT_RA_OUT, NOT_RB_IN,
       NOT_RB_OUT, NOT_RC_IN, NOT_RC_OUT, NOT_RD_IN, NOT_RD_OUT, NOT_RT_IN, NOT_RT_OUT, NOT_SP_CT, NOT_SP_IN,
       NOT_SP_OUT, NOT_SS_IN, NOT_SS_OUT, OP_SEL0, OP_SEL1, OP_SEL2, or_1_out, or_2_out, or_3_out, or_4_out,
       or_5_out, or_6_out, or_7_out, or_8_out, or_9_out, PHI1, PHI2, RA_S0, RA_S1, RESET, SP_DIR,
       SP_MODE_SEL0, SP_MODE_SEL1, switch_1_p2, ttyadapter_1_tty_we, X_SEL0, X_SEL1, X_SEL2, Y_SEL0, Y_SEL1,
       Y_SEL2;
  wire [2:0] alu_1_flags;
  wire [3:0] FLAGS_VAL;
  wire [6:0] bit_extender_1_out, keyboard_1_data;
  wire [7:0] ABH_q, ABL_q, aluoperandselector_1_o1, aluoperandselector_1_o2, aluoperatorselector_1_op_out,
       bufferedregister_1_async_out, controlunit_1_ir_out, DBUS, DL_VAL, FBUS, keyboardadapter_1_async_out,
       RA_VAL, RB_VAL, RC_VAL, RD_VAL, SP_VAL, SS_VAL, undriven, undriven_2, undriven_3;
  wire [15:0] ABUS, CS_PC;

  // Probe on controlunit_1_ir_out
  // Probe on CS_PC
  // Probe on ABUS
  // Probe on DBUS
  // Probe on RA_VAL
  // Probe on RB_VAL
  // Probe on RC_VAL
  // Probe on RD_VAL
  // Probe on DL_VAL
  // Probe on SS_VAL
  // Probe on SP_VAL
  // Probe on FLAGS_VAL
  // DipSwitch dipswitch_1: pin names not known
  assign DBUS = switch_1_p2 ? undriven : 8'bz;  // Controlled_Buffer controlled_buffer_1
  // Switch switch_1: pin names not known; wires that end beside it: 1'b1, switch_1_p2
  Pull_Resistor pull_resistor_1 (.node(switch_1_p2));
  Hex_Digit_Display hex_digit_display_1 (.value(DBUS[7:4]));  // open: dp
  Hex_Digit_Display hex_digit_display_2 (.value(DBUS[3:0]));  // open: dp
  ControlUnit controlunit_1 (
    .DBUS(DL_VAL), .NOT_IRQ(NOT_IRQ), .RESET(C1), .CLK(RESET), .I(FLAGS_VAL[3]),
    .IR_OUT(controlunit_1_ir_out), .RA_S0(RA_S0), .RA_S1(RA_S1), .NOT_RA_OUT(NOT_RA_OUT),
    .NOT_RB_IN(NOT_RB_IN), .NOT_RB_OUT(NOT_RB_OUT), .NOT_RC_IN(NOT_RC_IN), .NOT_RC_OUT(NOT_RC_OUT),
    .NOT_RD_IN(NOT_RD_IN), .NOT_RD_OUT(NOT_RD_OUT), .NOT_DEVICE_IN(NOT_DEVICE_IN),
    .NOT_DEVICE_OUT(NOT_DEVICE_OUT), .NOT_SS_IN(NOT_SS_IN), .NOT_SS_OUT(NOT_SS_OUT), .NOT_SP_IN(NOT_SP_IN),
    .NOT_SP_OUT(NOT_SP_OUT), .NOT_SP_CT(NOT_SP_CT), .SP_DIR(SP_DIR), .NOT_ABH_IN(NOT_ABH_IN),
    .NOT_ABL_IN(NOT_ABL_IN), .NOT_RT_IN(NOT_RT_IN), .NOT_RT_OUT(NOT_RT_OUT), .X_SEL0(X_SEL0),
    .X_SEL1(X_SEL1), .X_SEL2(X_SEL2), .Y_SEL0(Y_SEL0), .Y_SEL1(Y_SEL1), .Y_SEL2(Y_SEL2), .OP_SEL0(OP_SEL0),
    .OP_SEL1(OP_SEL1), .OP_SEL2(OP_SEL2), .NOT_CS_IN(NOT_CS_IN), .NOT_PC_IN(NOT_PC_IN),
    .NOT_PC_INC(NOT_PC_INC), .NOT_CS_OUT(NOT_CS_OUT), .NOT_PC_OUT(NOT_PC_OUT), .NOT_FETCH(NOT_FETCH), .J(J),
    .JC(JC), .JZ(JZ), .JN(JN), .JA(JA), .NOT_PASS(NOT_PASS), .NOT_HLT(NOT_HLT), .ADDR_SEL0(ADDR_SEL0),
    .ADDR_SEL1(ADDR_SEL1), .NOT_DATA_LATCH_OUT(NOT_DATA_LATCH_OUT), .NOT_IVH_OUT(NOT_IVH_OUT),
    .NOT_IVL_OUT(NOT_IVL_OUT), .FLAGS_MODE_SEL0(FLAGS_MODE_SEL0), .FLAGS_MODE_SEL1(FLAGS_MODE_SEL1),
    .FLAGS_MODE_SEL2(FLAGS_MODE_SEL2), .NOT_FLAGS_OUT(NOT_FLAGS_OUT), .CSPC_DIR(CSPC_DIR));
  LED led_1 (.in(RA_S0));
  LED led_2 (.in(RA_S1));
  LED led_3 (.in(NOT_RA_OUT));
  LED led_4 (.in(NOT_RB_IN));
  LED led_5 (.in(NOT_RB_OUT));
  LED led_6 (.in(NOT_RC_IN));
  LED led_7 (.in(NOT_RC_OUT));
  LED led_8 (.in(NOT_RD_IN));
  LED led_9 (.in(NOT_RD_OUT));
  LED led_10 (.in(NOT_DEVICE_IN));
  LED led_11 (.in(NOT_DEVICE_OUT));
  LED led_12 (.in(NOT_SS_IN));
  LED led_13 (.in(NOT_SS_OUT));
  LED led_14 (.in(NOT_SP_IN));
  LED led_15 (.in(NOT_SP_OUT));
  LED led_16 (.in(NOT_SP_CT));
  LED led_17 (.in(SP_DIR));
  LED led_18 (.in(NOT_ABH_IN));
  LED led_19 (.in(NOT_ABL_IN));
  LED led_20 (.in(NOT_RT_IN));
  LED led_21 (.in(NOT_RT_OUT));
  LED led_22 (.in(X_SEL0));
  LED led_23 (.in(X_SEL1));
  LED led_24 (.in(X_SEL2));
  LED led_25 (.in(Y_SEL0));
  LED led_26 (.in(Y_SEL1));
  LED led_27 (.in(Y_SEL2));
  LED led_28 (.in(OP_SEL0));
  LED led_29 (.in(OP_SEL1));
  LED led_30 (.in(OP_SEL2));
  LED led_31 (.in(NOT_CS_IN));
  LED led_32 (.in(NOT_PC_IN));
  LED led_33 (.in(NOT_PC_INC));
  LED led_34 (.in(NOT_CS_OUT));
  LED led_35 (.in(NOT_PC_OUT));
  LED led_36 (.in(NOT_FETCH));
  LED led_37 (.in(J));
  LED led_38 (.in(JC));
  LED led_39 (.in(JZ));
  LED led_40 (.in(JN));
  LED led_41 (.in(JA));
  LED led_42 (.in(NOT_PASS));
  LED led_43 (.in(NOT_HLT));
  LED led_44 (.in(ADDR_SEL0));
  LED led_45 (.in(ADDR_SEL1));
  LED led_46 (.in(NOT_DATA_LATCH_OUT));
  LED led_47 (.in(NOT_IVH_OUT));
  LED led_48 (.in(NOT_IVL_OUT));
  LED led_49 (.in(FLAGS_MODE_SEL0));
  LED led_50 (.in(FLAGS_MODE_SEL1));
  LED led_51 (.in(FLAGS_MODE_SEL2));
  LED led_52 (.in(NOT_FLAGS_OUT));
  LED led_53 (.in(CSPC_DIR));
  Pull_Resistor #(.pull(1)) pull_resistor_2 (.node(NOT_IRQ));
  or or_1 (or_1_out, NOT_DEVICE_SEL_0, NOT_DEVICE_IN);
  or or_2 (or_2_out, NOT_DEVICE_SEL_0, NOT_DEVICE_OUT);
  Keyboard keyboard_1 (
    .clk(keyboardadapter_1_k_clk), .re(keyboardadapter_1_k_read_en), .clr(keyboardadapter_1_k_clear),
    .avail(keyboard_1_avail), .data(keyboard_1_data));
  Hex_Digit_Display hex_digit_display_3 (.value(ABUS[15:12]));  // open: dp
  Hex_Digit_Display hex_digit_display_4 (.value(ABUS[11:8]));  // open: dp
  or or_3 (or_3_out, NOT_FETCH, NOT_DEVICE_SEL_0);
  Hex_Digit_Display hex_digit_display_5 (.value(ABUS[7:4]));  // open: dp
  Hex_Digit_Display hex_digit_display_6 (.value(ABUS[3:0]));  // open: dp
  Register ABH (.D(DBUS), .en(not_1_out), .clk(C3), .Q(ABH_q));  // open: clr
  not not_1 (not_1_out, NOT_ABH_IN);
  KeyboardAdapter keyboardadapter_1 (
    .K_AVAIL(keyboard_1_avail), .K_DATA(keyboard_1_data), .BUS_IN(DBUS), .ABUS(ABUS),
    .NOT_DEVICE_IN(or_1_out), .NOT_DEVICE_OUT(or_2_out), .CLK(C4), .NOT_IRQ(NOT_IRQ),
    .ASYNC_OUT(keyboardadapter_1_async_out), .K_READ_EN(keyboardadapter_1_k_read_en),
    .K_CLEAR(keyboardadapter_1_k_clear), .K_CLK(keyboardadapter_1_k_clk));
  Register ABL (.D(DBUS), .en(not_2_out), .clk(C3), .Q(ABL_q));  // open: clr
  not not_2 (not_2_out, NOT_ABL_IN);
  not not_3 (not_3_out, or_3_out);
  assign FBUS = not_3_out ? keyboardadapter_1_async_out : 8'bz;  // Controlled_Buffer controlled_buffer_2
  assign DBUS = not_4_out ? keyboardadapter_1_async_out : 8'bz;  // Controlled_Buffer controlled_buffer_3
  not not_4 (not_4_out, or_2_out);
  Pull_Resistor pull_resistor_3 (.node(RESET));
  // Switch RESET: pin names not known; wires that end beside it: 1'b1, RESET
  or or_4 (or_4_out, NOT_DEVICE_SEL_1, NOT_DEVICE_IN);
  or or_5 (or_5_out, NOT_DEVICE_SEL_1, NOT_DEVICE_OUT);
  Bit_Extender #(.out_width(7)) bit_extender_1 (.in(DBUS), .out(bit_extender_1_out));
  TTY #(.cols(56)) tty_1 (.data(bit_extender_1_out), .clk(C4), .we(ttyadapter_1_tty_we));  // open: clr
  Register SS (.D(DBUS), .en(not_5_out), .clk(C3), .Q(SS_VAL), .clr(1'b0));
  not not_5 (not_5_out, NOT_SS_IN);
  AddressSelector addressselector_1 (
    .ABL_in(ABL_q), .ABH_in(ABH_q), .SS_SP_in({SS_VAL, SP_VAL}), .CS_PC_in(CS_PC), .ADDR_SEL0(ADDR_SEL0),
    .ADDR_SEL1(ADDR_SEL1), .CSPC_override(PHI1), .ADDR_OUT(ABUS));
  or or_6 (or_6_out, NOT_FETCH, NOT_DEVICE_SEL_1);
  AddrDecoder addrdecoder_1 (
    .ABUS(ABUS), .NOT_DEVICE_SEL_ROM(NOT_DEVICE_SEL_ROM), .NOT_DEVICE_SEL_RAM(NOT_DEVICE_SEL_RAM),
    .NOT_DEVICE_SEL_0(NOT_DEVICE_SEL_0), .NOT_DEVICE_SEL_1(NOT_DEVICE_SEL_1),
    .NOT_DEVICE_SEL_2(NOT_DEVICE_SEL_2), .NOT_DEVICE_SEL_3(NOT_DEVICE_SEL_3),
    .NOT_DEVICE_SEL_4(NOT_DEVICE_SEL_4), .NOT_DEVICE_SEL_5(NOT_DEVICE_SEL_5));
  StackPointer SP (.SP_MODE_SEL0(SP_MODE_SEL0), .SP_MODE_SEL1(SP_MODE_SEL1), .CLK(C4), .DBUS(DBUS), .SP_OUT(SP_VAL));
  CodeSegment_ProgramCounter CSPC (
    .FLAGS(FLAGS_VAL), .J(J), .JC(JC), .JZ(JZ), .JN(JN), .JA(JA), .NOT_PC_IN(NOT_PC_IN),
    .NOT_CS_IN(NOT_CS_IN), .NOT_PC_INC(NOT_PC_INC), .RESET(RESET), .ABUS(ABUS), .CLK(C4),
    .NOT_PC_OUT(NOT_PC_OUT), .NOT_CS_OUT(NOT_CS_OUT), .CSPC_DIR(CSPC_DIR), .NOT_OE(PHI1), .CS_PC(CS_PC),
    .BUS_OUT(DBUS));
  TTYAdapter ttyadapter_1 (
    .DBUS_IN(DBUS), .ABUS(ABUS), .NOT_DEVICE_IN(or_4_out), .NOT_DEVICE_OUT(or_5_out), .CLK(C4),
    .TTY_WE(ttyadapter_1_tty_we));  // open: TTY_DATA, TTY_CLR
  not not_6 (not_6_out, or_6_out);
  assign FBUS = not_6_out ? undriven_2 : 8'bz;  // Controlled_Buffer controlled_buffer_4
  assign DBUS = not_7_out ? undriven_2 : 8'bz;  // Controlled_Buffer controlled_buffer_5
  not not_7 (not_7_out, or_5_out);
  Register DATA_LATCH (.D(DBUS), .en(not_8_out), .clk(C2), .Q(DL_VAL), .clr(RESET));
  not not_8 (not_8_out, NOT_FETCH);
  not not_9 (not_9_out, nor_1_out);
  assign DBUS = not_9_out ? DL_VAL : 8'bz;  // Controlled_Buffer controlled_buffer_6
  BufferedRegister bufferedregister_1 (
    .BUS_IN(DBUS), .CLK(C3), .NOT_R_IN(NOT_RT_IN), .NOT_R_OUT(NOT_RT_OUT), .NOT_ENABLE(PHI1),
    .ASYNC_OUT(bufferedregister_1_async_out), .BUS_OUT(DBUS));
  or or_7 (or_7_out, NOT_DEVICE_SEL_2, NOT_DEVICE_IN);
  or or_8 (or_8_out, NOT_DEVICE_SEL_2, NOT_DEVICE_OUT);
  TwoPhaseClock twophaseclock_1 (.NOT_HLT(NOT_HLT), .PHI1(PHI1), .PHI2(PHI2), .C1(C1), .C2(C2), .C3(C3), .C4(C4));
  RAMModule RAM (
    .ABUS(ABUS), .CLK(C3), .BUS_IN(DBUS), .NOT_DEVICE_IN(NOT_DEVICE_IN),
    .NOT_DEVICE_SEL_RAM(NOT_DEVICE_SEL_RAM), .NOT_DEVICE_OUT(NOT_DEVICE_OUT), .NOT_FETCH(NOT_FETCH),
    .DBUS_OUT(DBUS));  // open: PHI1, PHI2
  ROMModule rommodule_1 (
    .ABUS(ABUS), .NOT_DEVICE_OUT(NOT_DEVICE_OUT), .NOT_FETCH(NOT_FETCH), .PHI1(PHI1), .PHI2(PHI2),
    .NOT_DEVICE_SEL_ROM(NOT_DEVICE_SEL_ROM), .DBUS(DBUS));
  nor nor_1 (nor_1_out, PHI2, NOT_DATA_LATCH_OUT);
  nor nor_2 (nor_2_out, PHI1, NOT_IVL_OUT);
  assign DBUS = nor_2_out ? {8{1'b0}} : 8'bz;  // Controlled_Buffer controlled_buffer_7
  assign DBUS = nor_3_out ? 8'h1f : 8'bz;  // Controlled_Buffer controlled_buffer_8
  nor nor_3 (nor_3_out, PHI1, NOT_IVH_OUT);
  or or_9 (or_9_out, NOT_FETCH, NOT_DEVICE_SEL_2);
  not not_10 (not_10_out, or_9_out);
  assign FBUS = not_10_out ? undriven_3 : 8'bz;  // Controlled_Buffer controlled_buffer_9
  assign DBUS = not_11_out ? undriven_3 : 8'bz;  // Controlled_Buffer controlled_buffer_10
  not not_11 (not_11_out, or_8_out);
  BufferedRegister RC (
    .BUS_IN(DBUS), .CLK(C3), .NOT_R_IN(NOT_RC_IN), .NOT_R_OUT(NOT_RC_OUT), .NOT_ENABLE(PHI1),
    .ASYNC_OUT(RC_VAL), .BUS_OUT(DBUS));
  Hex_Digit_Display hex_digit_display_7 (.value(RC_VAL[7:4]));  // open: dp
  ShiftRegister RA (
    .S0(RA_S0), .S1(RA_S1), .CLK(C3), .BUS_IN(DBUS), .NOT_OE(NOT_RA_OUT), .NOT_ENABLE(PHI1),
    .ASYNC_OUT(RA_VAL), .BUS_OUT(DBUS));
  Hex_Digit_Display hex_digit_display_8 (.value(RA_VAL[7:4]));  // open: dp
  Hex_Digit_Display hex_digit_display_9 (.value(RC_VAL[3:0]));  // open: dp
  Hex_Digit_Display hex_digit_display_10 (.value(RA_VAL[3:0]));  // open: dp
  ALUOperandSelector aluoperandselector_1 (
    .X_SEL0(X_SEL0), .X_SEL1(X_SEL1), .X_SEL2(X_SEL2), .Y_SEL0(Y_SEL0), .Y_SEL1(Y_SEL1), .Y_SEL2(Y_SEL2),
    .A_ASYNC(RA_VAL), .B_ASYNC(RB_VAL), .C_ASYNC(RC_VAL), .D_ASYNC(RD_VAL),
    .E_ASYNC(bufferedregister_1_async_out), .F_ASYNC(8'h1), .O1(aluoperandselector_1_o1),
    .O2(aluoperandselector_1_o2));
  BufferedRegister RB (
    .BUS_IN(DBUS), .CLK(C3), .NOT_R_IN(NOT_RB_IN), .NOT_R_OUT(NOT_RB_OUT), .NOT_ENABLE(PHI1),
    .ASYNC_OUT(RB_VAL), .BUS_OUT(DBUS));
  BufferedRegister RD (
    .BUS_IN(DBUS), .CLK(C3), .NOT_R_IN(NOT_RD_IN), .NOT_R_OUT(NOT_RD_OUT), .NOT_ENABLE(PHI1),
    .ASYNC_OUT(RD_VAL), .BUS_OUT(DBUS));
  Hex_Digit_Display hex_digit_display_11 (.value(RD_VAL[7:4]));  // open: dp
  Hex_Digit_Display hex_digit_display_12 (.value(RD_VAL[3:0]));  // open: dp
  Hex_Digit_Display hex_digit_display_13 (.value(RB_VAL[7:4]));  // open: dp
  Hex_Digit_Display hex_digit_display_14 (.value(RB_VAL[3:0]));  // open: dp
  ALUOperatorSelector aluoperatorselector_1 (
    .OP_SEL0(OP_SEL0), .OP_SEL1(OP_SEL1), .OP_SEL2(OP_SEL2), .OP_OUT(aluoperatorselector_1_op_out));
  ALU alu_1 (
    .OPERATORS(aluoperatorselector_1_op_out), .O1(aluoperandselector_1_o1), .O2(aluoperandselector_1_o2),
    .NOT_ENABLE(PHI1), .BUS_OUT(DBUS), .FLAGS(alu_1_flags));
  FLAGSRegister FLAGS (
    .MODE2(FLAGS_MODE_SEL2), .MODE1(FLAGS_MODE_SEL1), .MODE0(FLAGS_MODE_SEL0), .BUS_IN(DBUS),
    .ALU_IN(alu_1_flags), .CLK(C3), .FLAGS_OUT(FLAGS_VAL));
  LED led_54 (.in(FLAGS_VAL[3]));
  LED led_55 (.in(FLAGS_VAL[2]));
  LED led_56 (.in(FLAGS_VAL[1]));
  LED led_57 (.in(FLAGS_VAL[0]));
  nor nor_4 (nor_4_out, PHI1, NOT_FLAGS_OUT);
  assign DBUS = nor_4_out ? {4'b0000, FLAGS_VAL} : 8'bz;  // Controlled_Buffer controlled_buffer_11

  // Notes on the sheet:
  //   IR
  //   CS_PC
  //   ABUS
  //   DBUS
  //   RA
  //   RB
  //   RC
  //   RD
  //   DL
  //   SS
  //   SP
  //   INZC
  //   Click here with the poke tool to type into the serial port ->
  //   Write to bus
  //   Data bus
  //   Address bus
  //   1. control 2. fetch 3. PC increment 4. data
  //   Clock
  //   RAM
  //   ROM
  //   DATA_LATCH
  //   RT
  //   RC
  //   RA
  //   ALU_OPERAND_SELECTOR
  //   RD
  //   RB
  //   ALU_OPERATOR_SELECTOR
  //   I
  //   N
  //   Z
  //   C
endmodule

module ShiftRegister (
  input  S0,
  input  S1,
  input  CLK,
  input  [7:0] BUS_IN,
  input  NOT_OE,
  input  NOT_ENABLE,
  output [7:0] ASYNC_OUT,
  output [7:0] BUS_OUT
);

  wire nor_1_out;

  nor nor_1 (nor_1_out, NOT_OE, NOT_ENABLE);
  L_4_bit_bidir_univ_shift_register_sn74194 l_4_bit_bidir_univ_shift_register_sn74194_1 (
    .SL_SERIAL(ASYNC_OUT[3]), .DATA_IN(BUS_IN[7:4]), .SR_SERIAL(1'b0), .CLK(CLK), .NOT_CLR(1'b1), .S0(S0),
    .S1(S1), .DATA_OUT(ASYNC_OUT[7:4]));
  L_4_bit_bidir_univ_shift_register_sn74194 l_4_bit_bidir_univ_shift_register_sn74194_2 (
    .SL_SERIAL(1'b0), .DATA_IN(BUS_IN[3:0]), .SR_SERIAL(ASYNC_OUT[4]), .CLK(CLK), .NOT_CLR(1'b1), .S0(S0),
    .S1(S1), .DATA_OUT(ASYNC_OUT[3:0]));
  assign BUS_OUT = nor_1_out ? ASYNC_OUT : 8'bz;  // Controlled_Buffer controlled_buffer_1
endmodule

module BufferedRegister (
  input  [7:0] BUS_IN,
  input  CLK,
  input  NOT_R_IN,
  input  NOT_R_OUT,
  input  NOT_ENABLE,
  output [7:0] ASYNC_OUT,
  output [7:0] BUS_OUT
);

  wire nor_1_out;

  Register register_1 (.D(BUS_IN), .en(NOT_R_IN), .clk(CLK), .Q(ASYNC_OUT), .clr(1'b0));
  nor nor_1 (nor_1_out, NOT_R_OUT, NOT_ENABLE);
  assign BUS_OUT = nor_1_out ? ASYNC_OUT : 8'bz;  // Controlled_Buffer controlled_buffer_1
endmodule

module ALUOperandSelector (
  input  X_SEL0,
  input  X_SEL1,
  input  X_SEL2,
  input  Y_SEL0,
  input  Y_SEL1,
  input  Y_SEL2,
  input  [7:0] A_ASYNC,
  input  [7:0] B_ASYNC,
  input  [7:0] C_ASYNC,
  input  [7:0] D_ASYNC,
  input  [7:0] E_ASYNC,
  input  [7:0] F_ASYNC,
  output [7:0] O1,
  output [7:0] O2
);

  wire decoder_1_out0, decoder_1_out1, decoder_1_out2, decoder_1_out3, decoder_1_out4, decoder_1_out5,
       decoder_2_out0, decoder_2_out1, decoder_2_out2, decoder_2_out3, decoder_2_out4, decoder_2_out5;

  Decoder #(.select(3)) decoder_1 (
    .out0(decoder_1_out0), .out1(decoder_1_out1), .out2(decoder_1_out2), .out3(decoder_1_out3),
    .out4(decoder_1_out4), .out5(decoder_1_out5), .sel({X_SEL2, X_SEL1, X_SEL0}), .en(1'b1));  // open: out6, out7
  Decoder #(.select(3)) decoder_2 (
    .out0(decoder_2_out0), .out1(decoder_2_out1), .out2(decoder_2_out2), .out3(decoder_2_out3),
    .out4(decoder_2_out4), .out5(decoder_2_out5), .sel({Y_SEL2, Y_SEL1, Y_SEL0}), .en(1'b1));  // open: out6, out7
  assign O2 = decoder_2_out2 ? C_ASYNC : 8'bz;  // Controlled_Buffer controlled_buffer_1
  assign O2 = decoder_2_out3 ? D_ASYNC : 8'bz;  // Controlled_Buffer controlled_buffer_2
  assign O2 = decoder_2_out4 ? E_ASYNC : 8'bz;  // Controlled_Buffer controlled_buffer_3
  assign O2 = decoder_2_out5 ? F_ASYNC : 8'bz;  // Controlled_Buffer controlled_buffer_4
  assign O2 = decoder_2_out0 ? A_ASYNC : 8'bz;  // Controlled_Buffer controlled_buffer_5
  assign O2 = decoder_2_out1 ? B_ASYNC : 8'bz;  // Controlled_Buffer controlled_buffer_6
  assign O1 = decoder_1_out0 ? A_ASYNC : 8'bz;  // Controlled_Buffer controlled_buffer_7
  assign O1 = decoder_1_out1 ? B_ASYNC : 8'bz;  // Controlled_Buffer controlled_buffer_8
  assign O1 = decoder_1_out2 ? C_ASYNC : 8'bz;  // Controlled_Buffer controlled_buffer_9
  assign O1 = decoder_1_out3 ? D_ASYNC : 8'bz;  // Controlled_Buffer controlled_buffer_10
  assign O1 = decoder_1_out4 ? E_ASYNC : 8'bz;  // Controlled_Buffer controlled_buffer_11
  assign O1 = decoder_1_out5 ? F_ASYNC : 8'bz;  // Controlled_Buffer controlled_buffer_12
endmodule

module ALUOperatorSelector (
  input  OP_SEL0,
  input  OP_SEL1,
  input  OP_SEL2,
  output [7:0] OP_OUT
);

  Decoder #(.select(3)) decoder_1 (
    .out0(OP_OUT[0]), .out1(OP_OUT[1]), .out2(OP_OUT[2]), .out3(OP_OUT[3]), .out4(OP_OUT[4]),
    .out5(OP_OUT[5]), .out6(OP_OUT[6]), .out7(OP_OUT[7]), .sel({OP_SEL2, OP_SEL1, OP_SEL0}), .en(1'b1));
endmodule

module FLAGSRegister (
  input  MODE2,
  input  MODE1,
  input  MODE0,
  input  [7:0] BUS_IN,
  input  [2:0] ALU_IN,
  input  CLK,
  output [3:0] FLAGS_OUT
);

  wire flagscontroller_1_c_val, flagscontroller_1_i_val, flagscontroller_1_n_val, flagscontroller_1_not_c_in,
       flagscontroller_1_not_i_in, flagscontroller_1_not_n_in, flagscontroller_1_not_z_in,
       flagscontroller_1_z_val;
  wire [3:0] bit_extender_1_out;

  Bit_Extender #(.out_width(4)) bit_extender_1 (.in(BUS_IN), .out(bit_extender_1_out));
  FLAGSController flagscontroller_1 (
    .MODE2(MODE2), .MODE1(MODE1), .MODE0(MODE0), .BUS_IN(bit_extender_1_out), .ALU_IN(ALU_IN),
    .NOT_C_IN(flagscontroller_1_not_c_in), .NOT_Z_IN(flagscontroller_1_not_z_in),
    .NOT_N_IN(flagscontroller_1_not_n_in), .NOT_I_IN(flagscontroller_1_not_i_in),
    .C_VAL(flagscontroller_1_c_val), .Z_VAL(flagscontroller_1_z_val), .N_VAL(flagscontroller_1_n_val),
    .I_VAL(flagscontroller_1_i_val));
  Register #(.width(1)) C (
    .D(flagscontroller_1_c_val), .en(flagscontroller_1_not_c_in), .clk(CLK), .Q(FLAGS_OUT[0]));  // open: clr
  Register #(.width(1)) Z (
    .D(flagscontroller_1_z_val), .en(flagscontroller_1_not_z_in), .clk(CLK), .Q(FLAGS_OUT[1]));  // open: clr
  Register #(.width(1)) N (
    .D(flagscontroller_1_n_val), .en(flagscontroller_1_not_n_in), .clk(CLK), .Q(FLAGS_OUT[2]));  // open: clr
  Register #(.width(1)) I (
    .D(flagscontroller_1_i_val), .en(flagscontroller_1_not_i_in), .clk(CLK), .Q(FLAGS_OUT[3]));  // open: clr
endmodule

module ALU (
  input  [7:0] OPERATORS,
  input  [7:0] O1,
  input  [7:0] O2,
  input  NOT_ENABLE,
  output [7:0] BUS_OUT,
  output [2:0] FLAGS
);

  wire adder_1_cout, and_2_out, and_3_out, nor_1_out, nor_2_out, nor_3_out, nor_4_out, not_2_out, or_2_out;
  wire [6:0] buffer_1_out;
  wire [7:0] adder_1_out, and_1_out, bit_extender_1_out, controlled_buffer_1_out, not_1_out, or_1_out,
       xor_1_out, xor_2_out;

  assign not_1_out = ~O1;  // NOT_Gate not_1, 8 bits wide
  assign xor_1_out = O1 ^ O2;  // XOR_Gate xor_1, 8 bits wide
  assign controlled_buffer_1_out = OPERATORS[6] ? not_1_out : 8'bz;  // Controlled_Buffer controlled_buffer_1
  assign controlled_buffer_1_out = OPERATORS[5] ? xor_1_out : 8'bz;  // Controlled_Buffer controlled_buffer_2
  assign and_1_out = O1 & O2;  // AND_Gate and_1, 8 bits wide
  assign controlled_buffer_1_out = OPERATORS[4] ? and_1_out : 8'bz;  // Controlled_Buffer controlled_buffer_3
  not not_2 (not_2_out, NOT_ENABLE);
  // NoConnect on OPERATORS[7]
  assign or_1_out = O1 | O2;  // OR_Gate or_1, 8 bits wide
  assign controlled_buffer_1_out = OPERATORS[3] ? or_1_out : 8'bz;  // Controlled_Buffer controlled_buffer_4
  nor nor_1 (nor_1_out, FLAGS[2], buffer_1_out[6]);
  assign bit_extender_1_out = {{7{OPERATORS[2]}}, OPERATORS[2]};  // Bit_Extender bit_extender_1
  assign {FLAGS[2], buffer_1_out} = controlled_buffer_1_out;  // Buffer buffer_1, 8 bits wide
  Pull_Resistor pull_resistor_1 (.node({FLAGS[2], buffer_1_out}));
  nor nor_2 (nor_2_out, buffer_1_out[5], buffer_1_out[4]);
  nor nor_3 (nor_3_out, buffer_1_out[3], buffer_1_out[2]);
  and and_2 (and_2_out, nor_1_out, nor_2_out);
  and and_3 (and_3_out, nor_3_out, nor_4_out);
  and and_4 (FLAGS[1], and_2_out, and_3_out);
  Adder adder_1 (.a(O1), .b(xor_2_out), .out(adder_1_out), .cin(OPERATORS[2]), .cout(adder_1_cout));
  assign xor_2_out = O2 ^ bit_extender_1_out;  // XOR_Gate xor_2, 8 bits wide
  assign controlled_buffer_1_out = or_2_out ? adder_1_out : 8'bz;  // Controlled_Buffer controlled_buffer_5
  xor xor_3 (FLAGS[0], OPERATORS[2], adder_1_cout);
  nor nor_4 (nor_4_out, buffer_1_out[1], buffer_1_out[0]);
  or or_2 (or_2_out, OPERATORS[2], OPERATORS[1]);
  assign BUS_OUT = not_2_out ? controlled_buffer_1_out : 8'bz;  // Controlled_Buffer controlled_buffer_6

  // Notes on the sheet:
  //   we invert the carry when subtracting, so that the carry flag in a sub operation means "borrow"
endmodule

module ClockModule (
  input  NOT_HLT,
  output C1,
  output C3,
  output C2,
  output C4
);

  wire and_1_out, and_2_out, CLK_GEN_out, nor_1_out, nor_2_out, nor_3_out, nor_4_out, not_1_out, not_2_out,
       not_3_out, not_4_out, not_5_out, not_6_out, not_7_out, not_8_out, not_9_out, not_10_out, not_11_out,
       not_12_out, sysclk_out;

  Clock #(.highDuration(2), .lowDuration(2), .phaseOffset(3)) CLK_GEN (.out(CLK_GEN_out));
  Clock #(.highDuration(2), .lowDuration(2), .phaseOffset(1)) sysclk (.out(sysclk_out));
  and and_1 (and_1_out, CLK_GEN_out, NOT_HLT);
  and and_2 (and_2_out, NOT_HLT, sysclk_out);
  nor nor_1 (nor_1_out, ~and_1_out, C3);  // NOR_Gate
  nor nor_2 (nor_2_out, C1, and_1_out);
  nor nor_3 (nor_3_out, ~and_2_out, C4);  // NOR_Gate
  nor nor_4 (nor_4_out, C2, and_2_out);
  not not_1 (not_1_out, nor_1_out);
  not not_2 (not_2_out, not_1_out);
  not not_3 (not_3_out, not_2_out);
  not not_4 (not_4_out, nor_2_out);
  not not_5 (not_5_out, not_4_out);
  not not_6 (not_6_out, not_5_out);
  not not_7 (not_7_out, nor_3_out);
  not not_8 (not_8_out, not_7_out);
  not not_9 (not_9_out, not_8_out);
  not not_10 (not_10_out, nor_4_out);
  not not_11 (not_11_out, not_10_out);
  not not_12 (not_12_out, not_11_out);
  not not_13 (C1, not_3_out);
  not not_14 (C3, not_6_out);
  not not_15 (C2, not_9_out);
  not not_16 (C4, not_12_out);
endmodule

module InstructionRegister (
);

  Counter counter_1 ();  // open: clr, load, up, count, clk, D, carry, Q
endmodule

module RAMModule (
  input  [15:0] ABUS,
  input  CLK,
  input  [7:0] BUS_IN,
  input  NOT_DEVICE_IN,
  input  NOT_DEVICE_SEL_RAM,
  input  NOT_DEVICE_OUT,
  input  NOT_FETCH,
  input  PHI1,
  input  PHI2,
  output [7:0] DBUS_OUT
);

  wire deviceoutputcontroller_1_not_device_oe, not_1_out, not_2_out, or_1_out;
  wire [7:0] ram_1_dout;
  wire [12:0] bit_extender_1_out;

  Bit_Extender #(.in_width(16), .out_width(13), .\type ("zero")) bit_extender_1 (.in(ABUS), .out(bit_extender_1_out));
  or or_1 (or_1_out, NOT_DEVICE_IN, NOT_DEVICE_SEL_RAM);
  RAM #(.addrWidth(13), .asyncread("true")) ram_1 (
    .addr(bit_extender_1_out), .we(not_1_out), .oe(1'b1), .clk(CLK), .din(BUS_IN), .dout(ram_1_dout));
  not not_1 (not_1_out, or_1_out);
  DeviceOutputController deviceoutputcontroller_1 (
    .NOT_DEVICE_OUT(NOT_DEVICE_OUT), .NOT_FETCH(NOT_FETCH), .PHI1(PHI1), .PHI2(PHI2),
    .NOT_DEVICE_SEL(NOT_DEVICE_SEL_RAM), .NOT_DEVICE_OE(deviceoutputcontroller_1_not_device_oe));
  assign DBUS_OUT = not_2_out ? ram_1_dout : 8'bz;  // Controlled_Buffer controlled_buffer_1
  not not_2 (not_2_out, deviceoutputcontroller_1_not_device_oe);
endmodule

module StackPointer (
  input  SP_MODE_SEL0,
  input  SP_MODE_SEL1,
  input  CLK,
  input  [7:0] DBUS,
  output [7:0] SP_OUT
);

  wire and_1_out, or_1_out;

  or or_1 (or_1_out, SP_MODE_SEL0, SP_MODE_SEL1);
  and and_1 (and_1_out, SP_MODE_SEL1, SP_MODE_SEL0);
  Counter counter_1 (
    .load(and_1_out), .up(SP_MODE_SEL0), .count(or_1_out), .clk(CLK), .D(DBUS), .Q(SP_OUT));  // open: clr, carry
  // also tied to GND on the sheet: {DBUS[0], DBUS[1], DBUS[2], DBUS[3], DBUS[4], DBUS[5], DBUS[6], DBUS[7]}

  // Notes on the sheet:
  //   SP_MODE_SEL
  //   00 - inactive
  //   01 - count up
  //   10 - count down
  //   11 - load
endmodule

module ROMModule (
  input  [15:0] ABUS,
  input  NOT_DEVICE_OUT,
  input  NOT_FETCH,
  input  PHI1,
  input  PHI2,
  input  NOT_DEVICE_SEL_ROM,
  output [7:0] DBUS
);

  wire deviceoutputcontroller_1_not_device_oe, not_1_out;
  wire [7:0] STORAGE_ROM_data;
  wire [12:0] bit_extender_1_out;

  Bit_Extender #(.in_width(16), .out_width(13), .\type ("zero")) bit_extender_1 (.in(ABUS), .out(bit_extender_1_out));
  ROM #(.addrWidth(13)) STORAGE_ROM (.addr(bit_extender_1_out), .data(STORAGE_ROM_data));
  DeviceOutputController deviceoutputcontroller_1 (
    .NOT_DEVICE_OUT(NOT_DEVICE_OUT), .NOT_FETCH(NOT_FETCH), .PHI1(PHI1), .PHI2(PHI2),
    .NOT_DEVICE_SEL(NOT_DEVICE_SEL_ROM), .NOT_DEVICE_OE(deviceoutputcontroller_1_not_device_oe));
  assign DBUS = not_1_out ? STORAGE_ROM_data : 8'bz;  // Controlled_Buffer controlled_buffer_1
  not not_1 (not_1_out, deviceoutputcontroller_1_not_device_oe);

  // Notes on the sheet:
  //   contents of STORAGE_ROM (hex, n*v repeats v):
  //   0 0 f9 8 21 7 0 f4 0 39 f8 f2 1 0 35 37 38 26 a4 ed 20 2b 60 0 dc eb 1d ee 11 db ee 11 40 3f 3d f6
  //   35 35 4*e4 f4 0 81 2b 60 0 3d f4 0 81 2b 60 0 3d f6 21 1 0 21 2 0 f6 36 1d 1 1e 2 75 ed 56 37 38 5
  //   3f 10 26 dc 1c 2 40 3f fa ee 57 fb 3e f6 2b 60 0 f6 6c 30 ec 7b 84 9 ec 80 ed 80 6c 11 ec 7b 84 5 ec
  //   7e ed 7e 6c 20 ec 7b 84 5 ec 7e ed 7e 3 ff f6 54 a f6 b4 f 84 a ec 8c 6c a 54 41 f6 54 30 f6 26 f4 0
  //   5d 84 ff ed c4 4*e3 b dc 26 f4 0 5d 84 ff ed c4 48 36 dc 26 f4 0 5d 84 ff ed c3 4*e3 b dc 26 f4 0 5d
  //   84 ff ed c3 48 dc fa 3d f6 3d fb f6 58*0 c1 5 3e cb 33 60 0 3e 33 60 0 20 f4 0 40 eb c 22 84 a ed 24
  //   84 8 ed 1d dc ee c 87 0 ed c e1 ee c e9 85 1 ed 47 85 4 eb f4 36 f4 0 8f eb f3 19 3 1a 4 3e 81 ed ab
  //   26 dc 84 2e ed 57 84 3a ed 6a ee f4 26 84 72 ed 52 84 52 ed 52 ee f4 1f 3 20 4 f3 85 9 ed 5d ee f4
  //   36 f4 0 8f eb f3 19 5 1a 6 3e ee b1 7b ed f8 eb f4 26 84 20 ed 76 ee f4 dc 26 36 63 85 2 eb f3 f4 0
  //   5d 84 ff ed f3 4*e3 b dc 26 dc f4 0 5d 84 ff ed f3 45 37 38 1f 3 20 4 22 dc 1c 4 eb a6 40 3f 3e ee
  //   6a db 1b 3 ee a1 34 3 5 34 4 6 1d 5 1e 6 1f 3 20 4 35 ee c4 35 14 b4 7 ed c4 ee d8 33 60 0 a 11 f4 0
  //   24 14 f4 0 24 33 60 0 3a 33 60 0 20 26 f4 0 24 33 60 0 20 3d 7c ed e6 ee eb 81 ed f8 ee eb dc eb f0
  //   ee bc db ee bc 3e 33 60 0 3f 33 60 0 a ee 7427*0 35 2f 40 0 84 0 ed 1a 2f 40 1 2b 60 0 37 38 5 3f 20
  //   1 22 dc 1c 1 40 3f 3d f7
endmodule

module CodeSegment_ProgramCounter (
  input  [3:0] FLAGS,
  input  J,
  input  JC,
  input  JZ,
  input  JN,
  input  JA,
  input  NOT_PC_IN,
  input  NOT_CS_IN,
  input  NOT_PC_INC,
  input  RESET,
  input  [15:0] ABUS,
  input  CLK,
  input  NOT_PC_OUT,
  input  NOT_CS_OUT,
  input  CSPC_DIR,
  input  NOT_OE,
  output [15:0] CS_PC,
  output [7:0] BUS_OUT
);

  wire and_1_out, and_2_out, and_3_out, and_4_out, and_5_out, nor_1_out, nor_2_out, nor_3_out, not_1_out,
       not_2_out, not_3_out, or_1_out, or_2_out, or_3_out, or_4_out, or_5_out, PC_carry;

  and and_1 (and_1_out, JC, FLAGS[0]);
  or or_1 (or_1_out, and_1_out, and_2_out);
  and and_2 (and_2_out, JZ, FLAGS[1]);
  and and_3 (and_3_out, JN, FLAGS[2]);
  or or_2 (or_2_out, and_3_out, and_4_out);
  or or_3 (or_3_out, or_1_out, or_2_out);
  nor nor_1 (nor_1_out, J, or_3_out);
  and and_4 (and_4_out, JA, FLAGS[3]);
  nor nor_2 (nor_2_out, NOT_CS_IN, nor_1_out);
  and and_5 (and_5_out, CLK, RESET);
  Counter CS (
    .clr(and_5_out), .load(nor_2_out), .up(CSPC_DIR), .count(PC_carry), .clk(CLK), .D(ABUS[15:8]),
    .Q(CS_PC[15:8]));  // open: carry
  not not_1 (not_1_out, NOT_PC_INC);
  nor nor_3 (nor_3_out, nor_1_out, NOT_PC_IN);
  Counter PC (
    .clr(and_5_out), .load(nor_3_out), .up(CSPC_DIR), .count(not_1_out), .clk(CLK), .D(ABUS[7:0]),
    .carry(PC_carry), .Q(CS_PC[7:0]));
  not not_2 (not_2_out, or_4_out);
  or or_4 (or_4_out, NOT_OE, NOT_PC_OUT);
  assign BUS_OUT = not_3_out ? CS_PC[15:8] : 8'bz;  // Controlled_Buffer controlled_buffer_1
  assign BUS_OUT = not_2_out ? CS_PC[7:0] : 8'bz;  // Controlled_Buffer controlled_buffer_2
  not not_3 (not_3_out, or_5_out);
  or or_5 (or_5_out, NOT_OE, NOT_CS_OUT);
endmodule

module LCD_emulator (
  input  RS,
  input  R_NW,
  input  LCD_EN,
  input  [7:0] BUS_IN
);
endmodule

module Interface_emulator (
  input  POLL,
  input  TRANSMIT,
  input  CLK,
  input  [7:0] BUS_IN,
  output [7:0] BUS_OUT,
  output A_OUT
);

  wire [7:0] register_1_q;

  Register register_1 (.D(BUS_IN), .en(TRANSMIT), .clk(CLK), .Q(register_1_q));  // open: clr
  assign BUS_OUT = POLL ? register_1_q : 8'bz;  // Controlled_Buffer controlled_buffer_1

  assign A_OUT = POLL;
endmodule

module ControlUnit (
  input  [7:0] DBUS,
  input  NOT_IRQ,
  input  RESET,
  input  CLK,
  input  I,
  output [7:0] IR_OUT,
  output RA_S0,
  output RA_S1,
  output NOT_RA_OUT,
  output NOT_RB_IN,
  output NOT_RB_OUT,
  output NOT_RC_IN,
  output NOT_RC_OUT,
  output NOT_RD_IN,
  output NOT_RD_OUT,
  output NOT_DEVICE_IN,
  output NOT_DEVICE_OUT,
  output NOT_SS_IN,
  output NOT_SS_OUT,
  output NOT_SP_IN,
  output NOT_SP_OUT,
  output NOT_SP_CT,
  output SP_DIR,
  output NOT_ABH_IN,
  output NOT_ABL_IN,
  output NOT_RT_IN,
  output NOT_RT_OUT,
  output X_SEL0,
  output X_SEL1,
  output X_SEL2,
  output Y_SEL0,
  output Y_SEL1,
  output Y_SEL2,
  output OP_SEL0,
  output OP_SEL1,
  output OP_SEL2,
  output NOT_CS_IN,
  output NOT_PC_IN,
  output NOT_PC_INC,
  output NOT_CS_OUT,
  output NOT_PC_OUT,
  output NOT_FETCH,
  output J,
  output JC,
  output JZ,
  output JN,
  output JA,
  output NOT_PASS,
  output NOT_HLT,
  output ADDR_SEL0,
  output ADDR_SEL1,
  output NOT_DATA_LATCH_OUT,
  output NOT_IVH_OUT,
  output NOT_IVL_OUT,
  output FLAGS_MODE_SEL0,
  output FLAGS_MODE_SEL1,
  output FLAGS_MODE_SEL2,
  output NOT_FLAGS_OUT,
  output CSPC_DIR
);

  wire n74163_1_pin3, n74163_1_pin10, not_1_out, or_1_out, or_2_out;
  wire [3:0] n74163_1_pin14;
  wire [7:0] multiplexer_1_out;
  wire [7:5] EEPROM6_data;

  not not_1 (not_1_out, NOT_PASS);
  Multiplexer #(.width(8)) multiplexer_1 (.in0(8'h2), .in1(DBUS), .out(multiplexer_1_out), .sel(or_1_out));
  or or_1 (or_1_out, NOT_IRQ, I);
  or or_2 (or_2_out, not_1_out, RESET);
  Register IR (.D(multiplexer_1_out), .en(or_2_out), .clk(CLK), .Q(IR_OUT), .clr(RESET));
  _74163 u_74163_1 (
    .pin1(or_2_out), .pin2(CLK), .pin3(n74163_1_pin3), .pin4(n74163_1_pin3), .pin5(n74163_1_pin3),
    .pin6(n74163_1_pin3), .pin7(n74163_1_pin3), .pin14(n74163_1_pin14[0]), .pin13(n74163_1_pin14[1]),
    .pin12(n74163_1_pin14[2]), .pin11(n74163_1_pin14[3]), .pin10(n74163_1_pin10), .pin9(n74163_1_pin10));  // open: pin15
  ROM #(.addrWidth(13)) EEPROM0 (
    .addr({1'b0, IR_OUT, n74163_1_pin14}),
    .data({NOT_RD_IN, NOT_RC_OUT, NOT_RC_IN, NOT_RB_OUT, NOT_RB_IN, NOT_RA_OUT, RA_S1, RA_S0}));
  ROM #(.addrWidth(13)) EEPROM1 (
    .addr({1'b0, IR_OUT, n74163_1_pin14}),
    .data({NOT_SP_CT, NOT_SP_OUT, NOT_SP_IN, NOT_SS_OUT, NOT_SS_IN, NOT_DEVICE_OUT, NOT_DEVICE_IN, NOT_RD_OUT}));
  ROM #(.addrWidth(13)) EEPROM2 (
    .addr({1'b0, IR_OUT, n74163_1_pin14}),
    .data({X_SEL2, X_SEL1, X_SEL0, NOT_RT_OUT, NOT_RT_IN, NOT_ABL_IN, NOT_ABH_IN, SP_DIR}));
  ROM #(.addrWidth(13)) EEPROM3 (
    .addr({1'b0, IR_OUT, n74163_1_pin14}),
    .data({NOT_PC_IN, NOT_CS_IN, OP_SEL2, OP_SEL1, OP_SEL0, Y_SEL2, Y_SEL1, Y_SEL0}));
  ROM #(.addrWidth(13)) EEPROM4 (
    .addr({1'b0, IR_OUT, n74163_1_pin14}),
    .data({JN, JZ, JC, J, NOT_FETCH, NOT_PC_OUT, NOT_CS_OUT, NOT_PC_INC}));
  ROM #(.addrWidth(13)) EEPROM5 (
    .addr({1'b0, IR_OUT, n74163_1_pin14}),
    .data({NOT_IVL_OUT, NOT_IVH_OUT, NOT_DATA_LATCH_OUT, ADDR_SEL1, ADDR_SEL0, NOT_HLT, NOT_PASS, JA}));
  ROM #(.addrWidth(13)) EEPROM6 (
    .addr({1'b0, IR_OUT, n74163_1_pin14}),
    .data({EEPROM6_data, CSPC_DIR, NOT_FLAGS_OUT, FLAGS_MODE_SEL2, FLAGS_MODE_SEL1, FLAGS_MODE_SEL0}));
  // also tied to VCC on the sheet: {n74163_1_pin3, n74163_1_pin10}

  // Notes on the sheet:
  //   Get the 163! Synchronous reset
  //   contents of EEPROM0 (hex, n*v repeats v):
  //   48*fc ff 15*fc f4 15*fc dc 15*fc 7c 47*fc 7c 15*fc 7c 15*fc f0 15*fc d8 15*fc 78 15*fc ef 15*fc cc
  //   15*fc 6c 15*fc bf 15*fc b4 15*fc 3c 15*fc ff 15*fc f4 15*fc dc 48*fc f8 15*fc ec 15*fc bc 31*fc ff
  //   15*fc f4 15*fc dc 15*fc 7c 30*fc bc fc f8 13*fc bc fc ec 13*fc bc fc bc 13*fc bc 15*fc bc fc ff
  //   13*fc bc fc f4 13*fc bc fc dc 13*fc bc fc 7c 13*fc bc 17*fc f8 15*fc ec 15*fc bc 31*fc ff 15*fc f4
  //   15*fc dc 15*fc 7c 45*fc f8 15*fc ec 15*fc bc 47*fc bc 47*fc ff 15*fc f4 15*fc dc 15*fc 7c 32*fc bc
  //   30*fc ff 15*fc ff 15*fc ff 15*fc ff 15*fc f4 15*fc f4 15*fc f4 15*fc f4 15*fc dc 15*fc dc 15*fc dc
  //   15*fc dc 15*fc 7c 15*fc 7c 15*fc 7c 15*fc 7c 16*fc ff 15*fc f4 15*fc f4 15*fc f4 78*fc ff 15*fc ff
  //   15*fc ff 15*fc ff 15*fc f4 15*fc f4 15*fc f4 15*fc f4 15*fc dc 15*fc dc 15*fc dc 15*fc dc 15*fc 7c
  //   15*fc 7c 15*fc 7c 15*fc 7c 16*fc ff 15*fc f4 15*fc f4 15*fc f4 462*fc ff 15*fc ff 15*fc ff 15*fc ff
  //   15*fc f4 15*fc f4 15*fc f4 15*fc f4 15*fc dc 15*fc dc 15*fc dc 15*fc dc 15*fc 7c 15*fc 7c 15*fc 7c
  //   15*fc 7c 16*fc ff 15*fc f4 15*fc f4 15*fc f4 78*fc ff 15*fc ff 15*fc ff 15*fc ff 15*fc f4 15*fc f4
  //   15*fc f4 15*fc f4 15*fc dc 15*fc dc 15*fc dc 15*fc dc 15*fc 7c 15*fc 7c 15*fc 7c 15*fc 7c 16*fc ff
  //   15*fc f4 15*fc f4 15*fc f4 78*fc ff 15*fc ff 15*fc ff 15*fc ff 15*fc f4 15*fc f4 15*fc f4 15*fc f4
  //   15*fc dc 15*fc dc 15*fc dc 15*fc dc 15*fc 7c 15*fc 7c 15*fc 7c 15*fc 7c 16*fc ff 15*fc f4 15*fc f4
  //   15*fc f4 78*fc ff 15*fc f4 15*fc dc 15*fc 7c 31*fc ff 15*fc f4 15*fc dc 15*fc 7c 31*fc ff 15*fc f4
  //   15*fc dc 15*fc 7c 31*fc fe 15*fc fd 15*fc f8 ef f4 13*fc f8 bf dc 13*fc f8 ff 7c 13*fc ec b4 dc
  //   13*fc ec f4 7c 13*fc bc dc 7c 141*fc bc 31*fc bc 4271*fc
  //   contents of EEPROM1 (hex, n*v repeats v):
  //   34*ff fd 7d 7d 7f 74*ff df 15*ff f7 15*ff ef 15*ff bf 159*ff fe 15*ff fe 15*ff fe 15*ff f6 15*ff de
  //   16*ff fd 15*ff fd 15*ff fd 15*ff fc 15*ff fb 15*ff fb 15*ff fb 15*ff fb 15*ff fd 15*ff fe fd 14*ff
  //   fe fd 14*ff fe fd 14*ff fe fc 14*ff fe fb 14*ff fe fb 14*ff fe fb 14*ff fe fb 14*ff fe fd 15*ff fd
  //   15*ff fd 15*ff fd 15*ff fc 15*ff fb 15*ff fb 15*ff fb 15*ff fb 15*ff fd 14*ff fb ff fd 12*ff fd 7f
  //   14*ff fd 7f 14*ff fd 7f 14*ff fc 7f 15*ff fb fd 7f 13*ff fe fb fd 7f 12*ff fe fb fd 7f 11*ff fd 7f
  //   14*ff 7b 15*ff 7b 15*ff 7b 15*ff 7b 16*ff 7b fd 13*ff 7b ff fe fd 12*ff 7b ff ff fd 333*ff fb fd
  //   14*ff fb fd 14*ff fb fd 14*ff fb fd 334*ff fb fd 14*ff fb fd 14*ff fb fd 14*ff fb fd 334*ff fb 15*ff
  //   fb 15*ff fb 15*ff fb 335*ff fb fd 14*ff fb fd 14*ff fb fd 14*ff fb fd 334*ff fb fd 14*ff fb fd 14*ff
  //   fb fd 14*ff fb fd 334*ff fb fd 14*ff fb fd 14*ff fb fd 14*ff fb fd 78*ff fb fd 78*ff fb fd 78*ff fb
  //   fd 78*ff fe 31*ff fe 15*ff fe 143*ff fe 16*ff fd 7d 7f 12*ff fe fd 7d 7f 11*ff 7b 7b 14*ff 7b 7b 7b
  //   4237*ff
  //   contents of EEPROM2 (hex, n*v repeats v):
  //   32*1e 1c 1a 1e 1f 1f 1f 362*1e 1a 15*1e 1a 15*1e 1a 15*1e 1a 15*1e 1a 15*1e 1a 15*1e 1a 15*1e 1a
  //   15*1e 1a 15*1e 1c 1a 14*1e 1c 1a 14*1e 1c 1a 14*1e 1c 1a 14*1e 1c 1a 14*1e 1c 1a 14*1e 1c 1a 14*1e
  //   1c 1a 14*1e 1c 1a 14*1e 1c 1a 14*1e 1c 1a 14*1e 1c 1a 14*1e 1c 1a 14*1e 1c 1a 14*1e 1c 1a 14*1e 1c
  //   1a 14*1e 1c 1a 14*1e 1c 1a 14*1e 1a 16 1a e 13*1e 1f 15*1e 1f 15*1e 1f 15*1e 1f 14*1e 1a 16 e 1f
  //   12*1e 1c 1a 16 e 1f 11*1e 1c 1a 16 e 1f 12*1e 1f 78*1e 1a 16 e 13*1e 16 1c 1a e 12*1e 16 1c 1a e
  //   76*1e 3e 15*1e 3e 15*1e 3e 15*1e 3e 15*1e 5e 15*1e 5e 15*1e 5e 15*1e 5e 15*1e 7e 15*1e 7e 15*1e 7e
  //   15*1e 7e 15*1e 16 15*1e 16 3e 14*1e 16 5e 14*1e 16 7e 14*1e 1a 16 9e 13*1e 1a 16 9e 13*1e 1a 16 9e
  //   13*1e 1a 16 9e 77*1e 3e 15*1e 3e 15*1e 3e 15*1e 3e 15*1e 5e 15*1e 5e 15*1e 5e 15*1e 5e 15*1e 7e
  //   15*1e 7e 15*1e 7e 15*1e 7e 15*1e 16 15*1e 16 3e 14*1e 16 5e 14*1e 16 7e 14*1e 1a 16 9e 13*1e 1a 16
  //   9e 13*1e 1a 16 9e 13*1e 1a 16 9e 77*1e 3e 15*1e 3e 15*1e 3e 15*1e 3e 15*1e 5e 15*1e 5e 15*1e 5e
  //   15*1e 5e 15*1e 7e 15*1e 7e 15*1e 7e 15*1e 7e 15*1e 16 15*1e 16 3e 14*1e 16 5e 14*1e 16 7e 14*1e 1a
  //   16 9e 13*1e 1a 16 9e 13*1e 1a 16 9e 13*1e 1a 16 9e 77*1e 3e 15*1e 3e 15*1e 3e 15*1e 3e 15*1e 5e
  //   15*1e 5e 15*1e 5e 15*1e 5e 15*1e 7e 15*1e 7e 15*1e 7e 15*1e 7e 15*1e 16 15*1e 16 3e 14*1e 16 5e
  //   14*1e 16 7e 14*1e 1a 16 9e 13*1e 1a 16 9e 13*1e 1a 16 9e 13*1e 1a 16 9e 77*1e 3e 15*1e 3e 15*1e 3e
  //   15*1e 3e 15*1e 5e 15*1e 5e 15*1e 5e 15*1e 5e 15*1e 7e 15*1e 7e 15*1e 7e 15*1e 7e 15*1e 16 15*1e 16
  //   3e 14*1e 16 5e 14*1e 16 7e 14*1e 1a 16 9e 13*1e 1a 16 9e 13*1e 1a 16 9e 13*1e 1a 16 9e 77*1e 3e
  //   15*1e 3e 15*1e 3e 15*1e 3e 15*1e 5e 15*1e 5e 15*1e 5e 15*1e 5e 15*1e 7e 15*1e 7e 15*1e 7e 15*1e 7e
  //   15*1e 16 15*1e 16 3e 14*1e 16 5e 14*1e 16 7e 14*1e 1a 16 9e 13*1e 1a 16 9e 13*1e 1a 16 9e 13*1e 1a
  //   16 9e 29*1e 3e 15*1e 5e 15*1e 7e 15*1e 1a 16 9e 29*1e 3e 15*1e 5e 15*1e 7e 15*1e 1a 16 9e 29*1e 3e
  //   15*1e 5e 15*1e 7e 15*1e 1a 16 9e 45*1e 16 1e e 13*1e 16 1e e 13*1e 16 1e e 13*1e 16 1e e 13*1e 16 1e
  //   e 13*1e 16 1e e 13*1e 1a 15*1e 1a 15*1e 1a 15*1e 1a 15*1e 1c 1a 14*1e 1c 1a 14*1e 1c 1a 14*1e 1c 1a
  //   14*1e 1c 1a 14*1e 1c 1a 1e 1f 1f 11*1e 1c 1a 1e 1f 1f 11*1e 1a 1c 15*1e 1a 1c 4237*1e
  //   contents of EEPROM3 (hex, n*v repeats v):
  //   37*c0 0 1050*c0 c8 15*c0 c9 15*c0 ca 15*c0 cb 15*c0 c8 15*c0 c9 15*c0 ca 15*c0 cb 15*c0 c8 15*c0 c9
  //   15*c0 ca 15*c0 cb 15*c0 c8 15*c0 c9 15*c0 ca 15*c0 cb 16*c0 cc 15*c0 cc 15*c0 cc 15*c0 cc 16*c0 c8
  //   15*c0 c9 15*c0 ca 15*c0 cb 13*c0 d0 15*c0 d1 15*c0 d2 15*c0 d3 15*c0 d0 15*c0 d1 15*c0 d2 15*c0 d3
  //   15*c0 d0 15*c0 d1 15*c0 d2 15*c0 d3 15*c0 d0 15*c0 d1 15*c0 d2 15*c0 d3 16*c0 d4 15*c0 d4 15*c0 d4
  //   15*c0 d4 16*c0 d0 15*c0 d1 15*c0 d2 15*c0 d3 13*c0 d0 15*c0 d1 15*c0 d2 15*c0 d3 15*c0 d0 15*c0 d1
  //   15*c0 d2 15*c0 d3 15*c0 d0 15*c0 d1 15*c0 d2 15*c0 d3 15*c0 d0 15*c0 d1 15*c0 d2 15*c0 d3 16*c0 d4
  //   15*c0 d4 15*c0 d4 15*c0 d4 16*c0 d0 15*c0 d1 15*c0 d2 15*c0 d3 13*c0 d8 15*c0 d9 15*c0 da 15*c0 db
  //   15*c0 d8 15*c0 d9 15*c0 da 15*c0 db 15*c0 d8 15*c0 d9 15*c0 da 15*c0 db 15*c0 d8 15*c0 d9 15*c0 da
  //   15*c0 db 16*c0 dc 15*c0 dc 15*c0 dc 15*c0 dc 16*c0 d8 15*c0 d9 15*c0 da 15*c0 db 13*c0 e0 15*c0 e1
  //   15*c0 e2 15*c0 e3 15*c0 e0 15*c0 e1 15*c0 e2 15*c0 e3 15*c0 e0 15*c0 e1 15*c0 e2 15*c0 e3 15*c0 e0
  //   15*c0 e1 15*c0 e2 15*c0 e3 16*c0 e4 15*c0 e4 15*c0 e4 15*c0 e4 16*c0 e0 15*c0 e1 15*c0 e2 15*c0 e3
  //   13*c0 e8 15*c0 e9 15*c0 ea 15*c0 eb 15*c0 e8 15*c0 e9 15*c0 ea 15*c0 eb 15*c0 e8 15*c0 e9 15*c0 ea
  //   15*c0 eb 15*c0 e8 15*c0 e9 15*c0 ea 15*c0 eb 16*c0 ec 15*c0 ec 15*c0 ec 15*c0 ec 16*c0 e8 15*c0 e9
  //   15*c0 ea 15*c0 eb 13*c0 f0 15*c0 f0 15*c0 f0 15*c0 f0 17*c0 f0 13*c0 cd 15*c0 cd 15*c0 cd 15*c0 cd
  //   17*c0 cd 13*c0 d5 15*c0 d5 15*c0 d5 15*c0 d5 17*c0 d5 142*c0 40 15*c0 40 15*c0 40 15*c0 40 16*c0 0
  //   15*c0 0 15*c0 0 15*c0 0 15*c0 0 17*c0 0 15*c0 0 13*c0 0 16*c0 0 4236*c0
  //   contents of EEPROM4 (hex, n*v repeats v):
  //   6 15*f 6 15*f e f d b f 1f 6 9*f 6 6 14*f 6 6 14*f 6 6 14*f 6 6 14*f 6 6 14*f 6 6 14*f 6 15*f 6 15*f
  //   6 15*f 6 15*f 6 15*f 6 15*f 6 15*f 6 15*f 6 15*f 6 15*f 6 15*f 6 15*f 6 15*f 6 15*f 6 15*f 6 15*f 6
  //   6 14*f 6 6 14*f 6 6 14*f 6 6 14*f 6 6 14*f 6 6 14*f 6 6 14*f 6 6 14*f 6 6 6 15*f 6 15*f 6 15*f 6
  //   15*f 6 15*f 6 15*f 6 15*f 6 15*f 6 15*f 6 6 12*f 6 6 6 13*f 6 6 6 13*f 6 6 6 13*f 6 6 6 13*f 6 6 6
  //   13*f 6 6 6 13*f 6 6 6 13*f 6 6 6 13*f 4*6 12*f 6 f 6 6 13*f 6 15*f 6 15*f 6 15*f 6 14*f 6 f f 6 16*f
  //   6 11*f 6 f f f 6 11*f 6 6 14*f 6 15*f 6 15*f 6 15*f 6 15*f 6 f 6 16*f 6 13*f 6 6 6 12*f 6 15*f 6
  //   15*f 6 15*f 6 15*f 6 15*f 6 15*f 6 15*f 6 15*f 6 15*f 6 15*f 6 15*f 6 15*f 6 15*f 6 15*f 6 15*f 6
  //   15*f 6 6 14*f 6 6 14*f 6 6 14*f 6 6 14*f 6 f 6 13*f 6 f 6 13*f 6 f 6 13*f 6 f 6 13*f 6 15*f 6 15*f 6
  //   15*f 6 15*f 6 15*f 6 15*f 6 15*f 6 15*f 6 15*f 6 15*f 6 15*f 6 15*f 6 15*f 6 15*f 6 15*f 6 15*f 6 6
  //   14*f 6 6 14*f 6 6 14*f 6 6 14*f 6 f 6 13*f 6 f 6 13*f 6 f 6 13*f 6 f 6 13*f 6 15*f 6 15*f 6 15*f 6
  //   15*f 6 15*f 6 15*f 6 15*f 6 15*f 6 15*f 6 15*f 6 15*f 6 15*f 6 15*f 6 15*f 6 15*f 6 15*f 6 6 14*f 6
  //   6 14*f 6 6 14*f 6 6 14*f 6 f 6 13*f 6 f 6 13*f 6 f 6 13*f 6 f 6 13*f 6 15*f 6 15*f 6 15*f 6 15*f 6
  //   15*f 6 15*f 6 15*f 6 15*f 6 15*f 6 15*f 6 15*f 6 15*f 6 15*f 6 15*f 6 15*f 6 15*f 6 6 14*f 6 6 14*f
  //   6 6 14*f 6 6 14*f 6 f 6 13*f 6 f 6 13*f 6 f 6 13*f 6 f 6 13*f 6 15*f 6 15*f 6 15*f 6 15*f 6 15*f 6
  //   15*f 6 15*f 6 15*f 6 15*f 6 15*f 6 15*f 6 15*f 6 15*f 6 15*f 6 15*f 6 15*f 6 6 14*f 6 6 14*f 6 6
  //   14*f 6 6 14*f 6 f 6 13*f 6 f 6 13*f 6 f 6 13*f 6 f 6 13*f 6 15*f 6 15*f 6 15*f 6 15*f 6 15*f 6 15*f
  //   6 15*f 6 15*f 6 15*f 6 15*f 6 15*f 6 15*f 6 15*f 6 15*f 6 15*f 6 15*f 6 6 14*f 6 6 14*f 6 6 14*f 6 6
  //   14*f 6 f 6 13*f 6 f 6 13*f 6 f 6 13*f 6 f 6 13*f 6 15*f 6 15*f 6 15*f 6 15*f 6 f 6 13*f 6 15*f 6
  //   15*f 6 15*f 6 15*f 6 f 6 13*f 6 15*f 6 15*f 6 15*f 6 15*f 6 f 6 13*f 6 15*f 6 17*f 6 15*f 6 15*f 6
  //   15*f 6 15*f 6 15*f 6 13*f 6 2f 6 13*f 6 8f 6 13*f 6 4f 6 13*f 6 1f 6 13*f 6 6 2f 6 12*f 6 6 8f 6
  //   12*f 6 6 4f 6 12*f 6 6 1f 6 14*f 1f 6 12*f 6 6 d b 1f 6 12*f d b 1f 6 12*f 1f 6 15*f 1f 6 11*f 6
  //   15*f 6 15*f 6 15*f 6 4175*f
  //   contents of EEPROM5 (hex, n*v repeats v):
  //   e4 15*e6 e0 15*e6 a6 66 f6 f6 f6 e6 e4 9*e6 c6 e4 14*e6 c6 e4 14*e6 c6 e4 14*e6 c6 e4 14*e6 c6 e4
  //   14*e6 c6 e4 14*e6 e4 15*e6 e4 15*e6 e4 15*e6 e4 15*e6 e4 15*e6 e4 15*e6 e4 15*e6 e4 15*e6 e4 15*e6
  //   e4 15*e6 e4 15*e6 e4 15*e6 e4 15*e6 e4 15*e6 e4 15*e6 e4 15*e6 c6 ec 14*e6 c6 ec 14*e6 c6 ec 14*e6
  //   c6 ec 14*e6 c6 ec 14*e6 c6 ec 14*e6 c6 ec 14*e6 c6 ec 14*e6 c6 ce e4 15*e6 e4 15*e6 e4 15*e6 e4
  //   15*e6 e4 15*e6 e4 15*e6 e4 15*e6 e4 15*e6 e4 15*e6 c6 e4 12*e6 c6 c6 e4 13*e6 c6 c6 e4 13*e6 c6 c6
  //   e4 13*e6 c6 c6 e4 13*e6 c6 c6 e4 13*e6 c6 c6 e4 13*e6 c6 c6 e4 13*e6 c6 c6 e4 13*e6 c6 c6 c6 e4
  //   12*e6 c6 ee c6 ec 12*e6 f6 e4 14*e6 f6 e4 14*e6 f6 e4 14*e6 f6 e4 14*e6 c6 ee f6 e4 15*e6 f6 e4
  //   11*e6 c6 e6 e6 f6 e4 11*e6 d6 e4 14*e6 f4 15*e6 f4 15*e6 f4 15*e6 f4 15*e6 c6 f6 ec 13*e6 f6 e6 e6
  //   e4 12*e6 f6 c6 c6 e4 12*e6 e4 15*e6 e4 15*e6 e4 15*e6 e4 15*e6 e4 15*e6 e4 15*e6 e4 15*e6 e4 15*e6
  //   e4 15*e6 e4 15*e6 e4 15*e6 e4 15*e6 e4 15*e6 e4 15*e6 e4 15*e6 e4 15*e6 c6 e4 14*e6 c6 e4 14*e6 c6
  //   e4 14*e6 c6 e4 14*e6 c6 ee ec 13*e6 c6 ee ec 13*e6 c6 ee ec 13*e6 c6 ee ec 13*e6 e4 15*e6 e4 15*e6
  //   e4 15*e6 e4 15*e6 e4 15*e6 e4 15*e6 e4 15*e6 e4 15*e6 e4 15*e6 e4 15*e6 e4 15*e6 e4 15*e6 e4 15*e6
  //   e4 15*e6 e4 15*e6 e4 15*e6 c6 e4 14*e6 c6 e4 14*e6 c6 e4 14*e6 c6 e4 14*e6 c6 ee ec 13*e6 c6 ee ec
  //   13*e6 c6 ee ec 13*e6 c6 ee ec 13*e6 e4 15*e6 e4 15*e6 e4 15*e6 e4 15*e6 e4 15*e6 e4 15*e6 e4 15*e6
  //   e4 15*e6 e4 15*e6 e4 15*e6 e4 15*e6 e4 15*e6 e4 15*e6 e4 15*e6 e4 15*e6 e4 15*e6 c6 e4 14*e6 c6 e4
  //   14*e6 c6 e4 14*e6 c6 e4 14*e6 c6 ee e4 13*e6 c6 ee e4 13*e6 c6 ee e4 13*e6 c6 ee e4 13*e6 e4 15*e6
  //   e4 15*e6 e4 15*e6 e4 15*e6 e4 15*e6 e4 15*e6 e4 15*e6 e4 15*e6 e4 15*e6 e4 15*e6 e4 15*e6 e4 15*e6
  //   e4 15*e6 e4 15*e6 e4 15*e6 e4 15*e6 c6 e4 14*e6 c6 e4 14*e6 c6 e4 14*e6 c6 e4 14*e6 c6 ee ec 13*e6
  //   c6 ee ec 13*e6 c6 ee ec 13*e6 c6 ee ec 13*e6 e4 15*e6 e4 15*e6 e4 15*e6 e4 15*e6 e4 15*e6 e4 15*e6
  //   e4 15*e6 e4 15*e6 e4 15*e6 e4 15*e6 e4 15*e6 e4 15*e6 e4 15*e6 e4 15*e6 e4 15*e6 e4 15*e6 c6 e4
  //   14*e6 c6 e4 14*e6 c6 e4 14*e6 c6 e4 14*e6 c6 ee ec 13*e6 c6 ee ec 13*e6 c6 ee ec 13*e6 c6 ee ec
  //   13*e6 e4 15*e6 e4 15*e6 e4 15*e6 e4 15*e6 e4 15*e6 e4 15*e6 e4 15*e6 e4 15*e6 e4 15*e6 e4 15*e6 e4
  //   15*e6 e4 15*e6 e4 15*e6 e4 15*e6 e4 15*e6 e4 15*e6 c6 e4 14*e6 c6 e4 14*e6 c6 e4 14*e6 c6 e4 14*e6
  //   c6 ee ec 13*e6 c6 ee ec 13*e6 c6 ee ec 13*e6 c6 ee ec 13*e6 e4 15*e6 e4 15*e6 e4 15*e6 e4 15*e6 c6
  //   ee ec 13*e6 e4 15*e6 e4 15*e6 e4 15*e6 e4 15*e6 c6 ee ec 13*e6 e4 15*e6 e4 15*e6 e4 15*e6 e4 15*e6
  //   c6 ee ec 13*e6 e4 15*e6 e4 17*e6 e4 15*e6 e4 15*e6 e4 15*e6 e4 15*e6 e4 15*e6 e4 13*e6 c6 e6 e4
  //   13*e6 c6 e6 e4 13*e6 c6 e6 e4 13*e6 c6 e6 e4 13*e6 c6 c6 e6 e4 12*e6 c6 c6 e6 e4 12*e6 c6 c6 e6 e4
  //   12*e6 c6 c6 e6 e4 15*e6 e4 12*e6 c6 c6 f6 f6 e6 e4 12*e6 f6 f6 e6 e4 10*e6 f6 f6 e6 e4 12*e6 f6 f6
  //   f6 e6 e4 11*e6 e4 15*e6 e4 15*e6 e4 15*e6 e4 4175*e6
  //   contents of EEPROM6 (hex, n*v repeats v):
  //   32*18 8 18 18 18 10 1d 1050*18 1b 15*18 1b 15*18 1b 15*18 1b 15*18 1b 15*18 1b 15*18 1b 15*18 1b
  //   15*18 1b 15*18 1b 15*18 1b 15*18 1b 15*18 1b 15*18 1b 15*18 1b 15*18 1b 16*18 1b 15*18 1b 15*18 1b
  //   15*18 1b 16*18 1b 15*18 1b 15*18 1b 15*18 1b 13*18 1b 15*18 1b 15*18 1b 15*18 1b 15*18 1b 15*18 1b
  //   15*18 1b 15*18 1b 15*18 1b 15*18 1b 15*18 1b 15*18 1b 15*18 1b 15*18 1b 15*18 1b 15*18 1b 16*18 1b
  //   15*18 1b 15*18 1b 15*18 1b 16*18 1b 15*18 1b 15*18 1b 15*18 1b 13*18 1b 15*18 1b 15*18 1b 15*18 1b
  //   15*18 1b 15*18 1b 15*18 1b 15*18 1b 15*18 1b 15*18 1b 15*18 1b 15*18 1b 15*18 1b 15*18 1b 15*18 1b
  //   15*18 1b 16*18 1b 15*18 1b 15*18 1b 15*18 1b 16*18 1b 15*18 1b 15*18 1b 15*18 1b 13*18 1b 15*18 1b
  //   15*18 1b 15*18 1b 15*18 1b 15*18 1b 15*18 1b 15*18 1b 15*18 1b 15*18 1b 15*18 1b 15*18 1b 15*18 1b
  //   15*18 1b 15*18 1b 15*18 1b 16*18 1b 15*18 1b 15*18 1b 15*18 1b 16*18 1b 15*18 1b 15*18 1b 15*18 1b
  //   13*18 1b 15*18 1b 15*18 1b 15*18 1b 15*18 1b 15*18 1b 15*18 1b 15*18 1b 15*18 1b 15*18 1b 15*18 1b
  //   15*18 1b 15*18 1b 15*18 1b 15*18 1b 15*18 1b 16*18 1b 15*18 1b 15*18 1b 15*18 1b 16*18 1b 15*18 1b
  //   15*18 1b 15*18 1b 13*18 1b 15*18 1b 15*18 1b 15*18 1b 15*18 1b 15*18 1b 15*18 1b 15*18 1b 15*18 1b
  //   15*18 1b 15*18 1b 15*18 1b 15*18 1b 15*18 1b 15*18 1b 15*18 1b 16*18 1b 15*18 1b 15*18 1b 15*18 1b
  //   16*18 1b 15*18 1b 15*18 1b 15*18 1b 13*18 1b 15*18 1b 15*18 1b 15*18 1b 17*18 1b 13*18 1b 15*18 1b
  //   15*18 1b 15*18 1b 17*18 1b 13*18 1b 15*18 1b 15*18 1b 15*18 1b 17*18 1b 333*18 1a 15*18 1c 15*18 1d
  //   15*18 1e 15*18 1f 4175*18
endmodule

module AddrDecoder (
  input  [15:0] ABUS,
  output NOT_DEVICE_SEL_ROM,
  output NOT_DEVICE_SEL_RAM,
  output NOT_DEVICE_SEL_0,
  output NOT_DEVICE_SEL_1,
  output NOT_DEVICE_SEL_2,
  output NOT_DEVICE_SEL_3,
  output NOT_DEVICE_SEL_4,
  output NOT_DEVICE_SEL_5
);

  wire decoder_1_out0, decoder_1_out1, decoder_1_out2, decoder_1_out3, decoder_1_out4, decoder_1_out5,
       decoder_1_out6, decoder_1_out7;

  Decoder #(.select(3)) decoder_1 (
    .out0(decoder_1_out0), .out1(decoder_1_out1), .out2(decoder_1_out2), .out3(decoder_1_out3),
    .out4(decoder_1_out4), .out5(decoder_1_out5), .out6(decoder_1_out6), .out7(decoder_1_out7),
    .sel(ABUS[15:13]), .en(1'b1));
  not not_1 (NOT_DEVICE_SEL_ROM, decoder_1_out0);
  not not_2 (NOT_DEVICE_SEL_RAM, decoder_1_out1);
  not not_3 (NOT_DEVICE_SEL_0, decoder_1_out2);
  not not_4 (NOT_DEVICE_SEL_1, decoder_1_out3);
  not not_5 (NOT_DEVICE_SEL_2, decoder_1_out4);
  not not_6 (NOT_DEVICE_SEL_3, decoder_1_out5);
  not not_7 (NOT_DEVICE_SEL_4, decoder_1_out6);
  not not_8 (NOT_DEVICE_SEL_5, decoder_1_out7);
endmodule

module AddressSelector (
  input  [7:0] ABL_in,
  input  [7:0] ABH_in,
  input  [15:0] SS_SP_in,
  input  [15:0] CS_PC_in,
  input  ADDR_SEL0,
  input  ADDR_SEL1,
  input  CSPC_override,
  output [15:0] ADDR_OUT
);

  wire [1:0] or_1_out;

  or or_1 (or_1_out[0], ADDR_SEL0, CSPC_override);
  or or_2 (or_1_out[1], ADDR_SEL1, CSPC_override);
  Multiplexer #(.select(2), .width(16)) multiplexer_1 (
    .in0({ABH_in, ABL_in}), .in1({8'h20, ABL_in}), .in2(SS_SP_in), .in3(CS_PC_in), .out(ADDR_OUT),
    .sel(or_1_out));

  // Notes on the sheet:
  //   01: 20:ABL
  //   10: SS:SP
  //   11: CS:PC
  //   00: ABH:ABL
endmodule

module FLAGSController (
  input  MODE2,
  input  MODE1,
  input  MODE0,
  input  [3:0] BUS_IN,
  input  [2:0] ALU_IN,
  output NOT_C_IN,
  output NOT_Z_IN,
  output NOT_N_IN,
  output NOT_I_IN,
  output C_VAL,
  output Z_VAL,
  output N_VAL,
  output I_VAL
);

  wire and_1_out, not_1_out, not_3_out, or_3_out, or_4_out, or_5_out, or_6_out, or_7_out, or_8_out, or_9_out,
       or_10_out, or_11_out, or_12_out, or_13_out, or_14_out, or_15_out;

  not not_1 (not_1_out, MODE2);
  not not_2 (NOT_C_IN, MODE1);
  not not_3 (not_3_out, MODE0);
  or or_1 (NOT_Z_IN, MODE2, NOT_C_IN);
  or or_2 (NOT_N_IN, MODE2, NOT_C_IN);
  or or_3 (or_3_out, not_1_out, MODE1);
  or or_4 (or_4_out, MODE2, NOT_C_IN);
  or or_5 (or_5_out, or_4_out, MODE0);
  or or_6 (or_6_out, MODE0, BUS_IN[0]);
  and and_1 (and_1_out, or_6_out, or_7_out);
  or or_7 (or_7_out, not_1_out, MODE0);
  or or_8 (or_8_out, MODE2, not_3_out);
  or or_9 (or_9_out, or_8_out, ALU_IN[0]);
  or or_10 (or_10_out, MODE0, BUS_IN[1]);
  and and_2 (Z_VAL, or_10_out, or_11_out);
  or or_11 (or_11_out, not_3_out, ALU_IN[1]);
  or or_12 (or_12_out, MODE0, BUS_IN[2]);
  and and_3 (N_VAL, or_12_out, or_13_out);
  or or_13 (or_13_out, not_3_out, ALU_IN[2]);
  or or_14 (or_14_out, MODE0, BUS_IN[3]);
  and and_4 (I_VAL, or_14_out, or_15_out);
  or or_15 (or_15_out, MODE1, MODE0);
  and and_5 (NOT_I_IN, or_3_out, or_5_out);
  and and_6 (C_VAL, and_1_out, or_9_out);
endmodule

module TwoPhaseClock (
  input  NOT_HLT,
  output PHI1,
  output PHI2,
  output C1,
  output C2,
  output C3,
  output C4
);

  wire and_1_out, clock_1_out, j_k_ff_1_q, not_1_out, not_2_out;

  Clock clock_1 (.out(clock_1_out));
  and and_1 (and_1_out, clock_1_out, NOT_HLT);
  J_K_Flip_Flop j_k_ff_1 (.J(1'b1), .K(1'b1), .clk(and_1_out), .Q(j_k_ff_1_q));  // open: Qn, preset, reset
  not not_1 (not_1_out, j_k_ff_1_q);
  not not_2 (not_2_out, and_1_out);
  J_K_Flip_Flop j_k_ff_2 (.J(not_1_out), .K(not_1_out), .clk(not_2_out), .Q(PHI1), .Qn(PHI2));  // open: preset, reset
  and and_2 (C1, j_k_ff_1_q, PHI1);
  and and_3 (C3, j_k_ff_1_q, PHI2);
  not not_3 (C2, C1);
  not not_4 (C4, C3);
endmodule

module DeviceOutputController (
  input  NOT_DEVICE_OUT,
  input  NOT_FETCH,
  input  PHI1,
  input  PHI2,
  input  NOT_DEVICE_SEL,
  output NOT_DEVICE_OE
);

  wire and_1_out, or_1_out, or_2_out;

  or or_1 (or_1_out, NOT_DEVICE_OUT, PHI1);
  and and_1 (and_1_out, or_1_out, or_2_out);
  or or_2 (or_2_out, NOT_FETCH, PHI2);
  or or_3 (NOT_DEVICE_OE, and_1_out, NOT_DEVICE_SEL);
endmodule
